# Fritzing sketch watch-winder (saved by Fritzing 0.9.5d)
circuit board: 10.7166cm x 7.36727cm

parts:
  Pico_H1 = Raspberry Pi Pico H
  Driver1 = 28BYJ-48 Driver Module [part_number=ULN2003 package=THT]
  SM1 = 28BYJ-48 Stepper Motor [part_number=28BYJ-48]
  Driver2 = 28BYJ-48 Driver Module [part_number=ULN2003 package=THT]
  SM2 = 28BYJ-48 Stepper Motor [part_number=28BYJ-48]
  Mode_3-Way_Slideswitch = SWITCH-DPDT [package=mss22]
  Turbo-Button_1 = Round Pushbutton
  Turbo-Button_0 = Round Pushbutton

nets:
  GND: Pico_H1.GND, Driver1.GND, Driver2.GND, Mode_3-Way_Slideswitch.5, Turbo-Button_1.leg0, Turbo-Button_0.leg1
  N1: Pico_H1.GP13, Mode_3-Way_Slideswitch.4
  N2: Pico_H1.GP12, Mode_3-Way_Slideswitch.6
  N3: Pico_H1.GP11, Turbo-Button_1.leg1
  N4: Pico_H1.GP10, Turbo-Button_0.leg0
  N5: Pico_H1.GP9, Driver1.IN4
  N6: Pico_H1.GP8, Driver1.IN2
  N7: Pico_H1.GP7, Driver1.IN3
  N8: Pico_H1.GP6, Driver1.IN1
  N9: Pico_H1.GP5, Driver2.IN4
  N10: Pico_H1.GP4, Driver2.IN2
  N11: Pico_H1.GP3, Driver2.IN3
  N12: Pico_H1.GP2, Driver2.IN1
  5V: Pico_H1.GP0, Driver1.Vmotor, Driver2.Vmotor
  N13: Driver1.blue-pin, SM1.blue-pin
  N14: Driver1.pink-pin, SM1.pink-pin
  N15: Driver1.yellow-pin, SM1.yellow-pin
  N16: Driver1.orange-pin, SM1.orange-pin
  N17: Driver1.red-pin, SM1.red-pin
  N18: Driver2.blue-pin, SM2.blue-pin
  N19: Driver2.pink-pin, SM2.pink-pin
  N20: Driver2.yellow-pin, SM2.yellow-pin
  N21: Driver2.orange-pin, SM2.orange-pin
  N22: Driver2.red-pin, SM2.red-pin

custom parts:
  Raspberry Pi Pico H: Raspberry Pi Pico H. Based around the RP2040 microcontroller the Pico H is a low cost microcontroller device bringing Raspberry Pi quality, cost, and easy of use to the microcontroller space.
  28BYJ-48 Driver Module: ULN2003 Driver Module for the 28BYJ-48 Unipolar Stepper Motor LED A - Blue wire - Bottom coil left LED B - Pink wire - Top coil left LED C - Yellow wire - Bottom coil right LED D - Orange wire - Top coil right Common rail - red Connector pins: blue - pink - yellow - orange - red Control pins - IN1 to IN4 Power pins - GND & Vmotor (5-12V) On/Off jumper (if removed, power to motor is cut).
  28BYJ-48 Stepper Motor: Unipolar Stepper Motor 28BYJ-48 Top coil - pink & orange Bottom coil - blue & yellow Common rail - red Connector pins: blue - pink - yellow - orange - red
